// Logisim project TrabGB.circ as structural Verilog: 6 circuits, main circuit main
module main (
  input  start,
  input  [3:0] A,
  input  [3:0] B,
  output [2:0] out_4
);

  wire clock_out, contador_tc, datapath_out_4, FSM_ic, reset_out;
  wire [1:0] FSM_display;
  wire [2:0] FSM_cont;
  wire [6:0] datapath_a_2, datapath_b_2;

  Clock clock (.out(clock_out));
  \máquina_de_estados  FSM (
    .TC(contador_tc), .start(start), .A_B(datapath_out_4), .cont(FSM_cont), .IC(FSM_ic),
    .Display(FSM_display), .clock(clock_out), .reset(reset_out));
  Button reset (.out(reset_out));
  contador contador (.atual(out_4), .valor(FSM_cont), .clock(clock_out), .IC(FSM_ic), .TC(contador_tc));
  datapath datapath (
    .A(A), .B(B), .out_4(datapath_out_4), .estado(FSM_display), .A_2(datapath_a_2), .B_2(datapath_b_2));
  _7_Segment_Display u_7_segment_display_1 (
    .g(datapath_a_2[6]), .f(datapath_a_2[5]), .a(datapath_a_2[0]), .b(datapath_a_2[1]), .e(datapath_a_2[4]),
    .d(datapath_a_2[3]), .c(datapath_a_2[2]));  // open: dp
  _7_Segment_Display u_7_segment_display_2 (
    .g(datapath_b_2[6]), .f(datapath_b_2[5]), .a(datapath_b_2[0]), .b(datapath_b_2[1]), .e(datapath_b_2[4]),
    .d(datapath_b_2[3]), .c(datapath_b_2[2]));  // open: dp
endmodule

module \máquina_de_estados  (
  input  TC,
  input  start,
  input  A_B,
  input  clock,
  input  reset,
  output IC,
  output [2:0] cont,
  output [1:0] Display
);

  wire e0_1_pe0, e1_1_pe1, not_1_out, register_2_q;

  E1 e1_1 (.E1(cont[0]), .E0(register_2_q), .TC(TC), .PE1(e1_1_pe1));
  E0 e0_1 (.E1(cont[0]), .E0(register_2_q), .S(start), .TC(TC), .A_B(A_B), .PE0(e0_1_pe0));
  Register #(.width(1)) register_1 (.D(e1_1_pe1), .Q(cont[0]), .clk(clock), .clr(reset));  // open: en
  Register #(.width(1)) register_2 (.D(e0_1_pe0), .Q(register_2_q), .clk(clock), .clr(reset));  // open: en
  not not_1 (not_1_out, cont[0]);
  or or_1 (IC, cont[0], register_2_q);
  or or_2 (cont[1], cont[0], register_2_q);
  and and_1 (cont[2], not_1_out, register_2_q);
  buf buffer_1 (Display[1], cont[0]);
  buf buffer_2 (Display[0], register_2_q);
endmodule

module E1 (
  input  E1,
  input  E0,
  input  TC,
  output PE1
);

  wire E1_E0_out, E1_TC_out, E1E0TC_out, not_1_out, not_2_out, not_3_out;

  not not_1 (not_1_out, E1);
  not not_2 (not_2_out, E0);
  not not_3 (not_3_out, TC);
  and E1E0TC (E1E0TC_out, not_1_out, E0, TC);
  and E1_E0 (E1_E0_out, E1, not_2_out);
  and E1_TC (E1_TC_out, E1, not_3_out);
  or or_1 (PE1, E1E0TC_out, E1_E0_out, E1_TC_out);
endmodule

module E0 (
  input  E1,
  input  E0,
  input  S,
  input  TC,
  input  A_B,
  output PE0
);

  wire E0_TC_out, E1_E0S_out, E1E0TC_A_B_out, not_1_out, not_2_out, not_3_out, not_4_out, not_5_out;

  not not_1 (not_1_out, E1);
  and E1_E0S (E1_E0S_out, not_1_out, not_2_out, S);
  not not_2 (not_2_out, E0);
  not not_3 (not_3_out, TC);
  and E0_TC (E0_TC_out, not_3_out, E0);
  not not_4 (not_4_out, E1);
  and E1E0TC_A_B (E1E0TC_A_B_out, not_4_out, E0, TC, not_5_out);
  not not_5 (not_5_out, A_B);
  or or_1 (PE0, E1_E0S_out, E0_TC_out, E1E0TC_A_B_out);
endmodule

module datapath (
  input  [1:0] estado,
  input  [3:0] A,
  input  [3:0] B,
  output out_4,
  output [6:0] A_2,
  output [6:0] B_2
);

  wire [3:0] gray_2_p3, gray_p3, multiplexer_1_out, multiplexer_2_out, somador_p3;

  // conversorGray_main gray: pin names not known; wires that end beside it: 1'b1, A, gray_p3
  // conversorGray_main gray_2: pin names not known; wires that end beside it: 1'b1, B, gray_2_p3
  // somador_main somador: pin names not known; wires that end beside it: A, B, somador_p3, 1'b1
  Multiplexer #(.select(2), .width(4), .enable("false")) multiplexer_1 (
    .in0(4'b1111), .in1(A), .in2(somador_p3), .in3(gray_p3), .out(multiplexer_1_out), .sel(estado));
  Multiplexer #(.select(2), .width(4), .enable("false")) multiplexer_2 (
    .in0(4'b1111), .in1(B), .in2(4'b1111), .in3(gray_2_p3), .out(multiplexer_2_out), .sel(estado));
  // bin_to_7seg display_A: pin names not known; wires that end beside it: A_2[0], A_2[1], A_2[2], A_2[3], A_2[4], A_2[5], A_2[6]
  // bin_to_7seg display_B: pin names not known; wires that end beside it: B_2[0], B_2[1], B_2[2], B_2[3], B_2[4], B_2[5], B_2[6]
  // Trabalho_Arquitetura___Combinacional_main comparador: pin names not known; wires that end beside it: A[3], A[2], A[1], A[0], B[3], B[2], B[1], B[0], out_4
endmodule

module contador (
  input  [2:0] valor,
  input  clock,
  input  IC,
  output TC,
  output [2:0] atual
);

  wire not_1_out, xnor_1_out, xnor_2_out, xnor_3_out;

  Counter #(.width(3), .max('h6)) contador (
    .D(valor), .count(IC), .Q(atual), .clk(clock), .clr(not_1_out));  // open: load, carry
  not not_1 (not_1_out, IC);
  xnor xnor_1 (xnor_1_out, valor[0], atual[0]);
  xnor xnor_2 (xnor_2_out, valor[1], atual[1]);
  xnor xnor_3 (xnor_3_out, valor[2], atual[2]);
  and and_1 (TC, xnor_1_out, xnor_2_out, xnor_3_out);
endmodule
