// Logisim project circuito 1 final pronto.circ as structural Verilog: 2 circuits, main circuit main
module main (
  input  A,
  input  B,
  input  [3:0] A_2,
  input  C,
  input  [3:0] B_2,
  input  D,
  input  in_7
);

  wire and_1_out, and_2_out, and_3_out, and_4_out, and_5_out, and_6_out, and_7_out, and_8_out, and_9_out,
       and_10_out, and_11_out, and_12_out, and_13_out, and_14_out, and_15_out, and_16_out, and_17_out,
       and_18_out, and_19_out, and_20_out, and_21_out, and_22_out, and_23_out, and_24_out, and_25_out,
       and_26_out, and_27_out, and_28_out, and_29_out, and_30_out, and_31_out, not_1_out, not_2_out,
       not_3_out, not_4_out, not_5_out, not_6_out, not_7_out, not_8_out, not_9_out, not_10_out, not_11_out,
       not_12_out, not_13_out, not_14_out, not_15_out, not_16_out, not_17_out, not_18_out, not_19_out,
       not_20_out, not_21_out, not_22_out, not_23_out, not_24_out, not_25_out, not_26_out, not_27_out,
       not_28_out, not_29_out, not_30_out, not_31_out, not_32_out, not_33_out, not_34_out, not_35_out,
       not_36_out, or_1_out, or_2_out, or_3_out, or_4_out, or_5_out, or_6_out, or_7_out, or_8_out, or_9_out;
  wire [3:0] multiplexer_1_out;
  wire [6:0] chip_1_a_2, demultiplexer_1_out0, demultiplexer_1_out1;

  Multiplexer #(.width(4), .disabled(0), .enable("false")) multiplexer_1 (
    .in0(A_2), .in1(B_2), .out(multiplexer_1_out), .sel(in_7));
  chip chip_1 (
    .A(multiplexer_1_out[3]), .B(multiplexer_1_out[2]), .C(multiplexer_1_out[1]), .D(multiplexer_1_out[0]),
    .a_2(chip_1_a_2[0]), .b_2(chip_1_a_2[1]), .c_2(chip_1_a_2[2]), .d_2(chip_1_a_2[3]),
    .out_9(chip_1_a_2[4]), .f(chip_1_a_2[5]), .g(chip_1_a_2[6]));
  Demultiplexer #(.width(7), .enable("false")) demultiplexer_1 (
    .out0(demultiplexer_1_out0), .out1(demultiplexer_1_out1), .in(chip_1_a_2), .sel(in_7));
  _7_Segment_Display u_7_segment_display_1 (
    .g(demultiplexer_1_out0[6]), .f(demultiplexer_1_out0[5]), .a(demultiplexer_1_out0[0]),
    .b(demultiplexer_1_out0[1]), .e(demultiplexer_1_out0[4]), .d(demultiplexer_1_out0[3]),
    .c(demultiplexer_1_out0[2]));  // open: dp
  _7_Segment_Display u_7_segment_display_2 (
    .g(demultiplexer_1_out1[6]), .f(demultiplexer_1_out1[5]), .a(demultiplexer_1_out1[0]),
    .b(demultiplexer_1_out1[1]), .e(demultiplexer_1_out1[4]), .d(demultiplexer_1_out1[3]),
    .c(demultiplexer_1_out1[2]));  // open: dp
  not not_1 (not_1_out, A);
  not not_2 (not_2_out, B);
  not not_3 (not_3_out, C);
  and and_1 (and_1_out, B, D, not_1_out);
  and and_2 (and_2_out, not_1_out, C);
  not not_4 (not_4_out, B);
  not not_5 (not_5_out, D);
  and and_3 (and_3_out, not_4_out, not_6_out, A);
  not not_6 (not_6_out, C);
  not not_7 (not_7_out, C);
  not not_8 (not_8_out, B);
  not not_9 (not_9_out, D);
  not not_10 (not_10_out, A);
  not not_11 (not_11_out, not_2_out);
  not not_12 (not_12_out, A);
  not not_13 (not_13_out, A);
  not not_14 (not_14_out, D);
  not not_15 (not_15_out, B);
  not not_16 (not_16_out, C);
  not not_17 (not_17_out, D);
  not not_18 (not_18_out, B);
  not not_19 (not_19_out, A);
  not not_20 (not_20_out, C);
  and and_4 (and_4_out, not_4_out, not_5_out);
  and and_5 (and_5_out, not_7_out, not_8_out);
  and and_6 (and_6_out, not_8_out, not_9_out);
  and and_7 (and_7_out, not_7_out, not_9_out, not_10_out);
  and and_8 (and_8_out, not_10_out, C, D);
  and and_9 (and_9_out, A, not_2_out);
  and and_10 (and_10_out, not_11_out, not_12_out);
  and and_11 (and_11_out, not_12_out, not_3_out);
  and and_12 (and_12_out, not_12_out, D);
  and and_13 (and_13_out, not_13_out, not_14_out, C);
  or or_1 (or_1_out, and_13_out, and_14_out);
  and and_14 (and_14_out, not_15_out, C, D);
  and and_15 (and_15_out, A, not_16_out, not_17_out);
  and and_16 (and_16_out, not_16_out, not_17_out, not_18_out);
  and and_17 (and_17_out, not_18_out, A, D);
  and and_18 (and_18_out, not_19_out, B, not_20_out, D);
  or or_2 (or_2_out, and_1_out, and_2_out, and_4_out, and_3_out);
  or or_3 (or_3_out, and_5_out, and_6_out, and_7_out, and_8_out);
  or or_4 (or_4_out, and_9_out, and_10_out, and_11_out, and_12_out);
  or or_5 (or_5_out, or_1_out, and_15_out, and_16_out, and_17_out, and_18_out);
  not not_21 (not_21_out, B);
  not not_22 (not_22_out, D);
  not not_23 (not_23_out, A);
  not not_24 (not_24_out, C);
  not not_25 (not_25_out, B);
  not not_26 (not_26_out, A);
  not not_27 (not_27_out, C);
  not not_28 (not_28_out, D);
  not not_29 (not_29_out, B);
  not not_30 (not_30_out, C);
  not not_31 (not_31_out, D);
  not not_32 (not_32_out, B);
  not not_33 (not_33_out, A);
  not not_34 (not_34_out, C);
  not not_35 (not_35_out, D);
  not not_36 (not_36_out, A);
  _7_Segment_Display u_7_segment_display_3 (
    .g(or_8_out), .f(or_7_out), .a(or_2_out), .b(or_3_out), .e(or_6_out), .d(or_5_out), .c(or_4_out));  // open: dp
  and and_19 (and_19_out, not_21_out, not_22_out);
  and and_20 (and_20_out, not_22_out, not_23_out, C);
  and and_21 (and_21_out, A, not_24_out, not_22_out);
  and and_22 (and_22_out, A, not_21_out, C);
  and and_23 (and_23_out, A, not_25_out);
  and and_24 (and_24_out, not_26_out, not_27_out, B);
  and and_25 (and_25_out, not_26_out, B, not_28_out);
  and and_26 (and_26_out, not_29_out, not_30_out, not_31_out);
  and and_27 (and_27_out, A, not_32_out);
  and and_28 (and_28_out, not_32_out, C);
  and and_29 (and_29_out, not_33_out, B, not_34_out);
  and and_30 (and_30_out, B, not_34_out, not_35_out);
  and and_31 (and_31_out, not_36_out, C, not_35_out);
  or or_6 (or_6_out, and_19_out, and_20_out, and_21_out, and_22_out);
  or or_7 (or_7_out, and_23_out, and_24_out, and_25_out, and_26_out);
  or or_8 (or_8_out, and_27_out, and_28_out, and_29_out, or_9_out);
  or or_9 (or_9_out, and_30_out, and_31_out);

  // Notes on the sheet:
  //   A
  //   B
  //   C
  //   D
  //   A
  //   B
  //   C
  //   D
  //   D
  //   A
  //   B
  //   C
  //   A
  //   B
  //   C
  //   D
  //   a
  //   b
  //   c
  //   d
  //   e
  //   f
  //   g
endmodule

module chip (
  input  A,
  input  B,
  input  C,
  input  D,
  output a_2,
  output b_2,
  output c_2,
  output d_2,
  output out_9,
  output f,
  output g
);

  wire and_1_out, and_2_out, and_3_out, and_4_out, and_5_out, and_6_out, and_7_out, and_8_out, and_9_out,
       and_10_out, and_11_out, and_12_out, and_13_out, and_14_out, and_15_out, and_16_out, and_17_out,
       and_18_out, and_19_out, and_20_out, and_21_out, and_22_out, and_23_out, and_24_out, and_25_out,
       and_26_out, and_27_out, and_28_out, and_29_out, and_30_out, and_31_out, not_1_out, not_2_out,
       not_3_out, not_4_out, not_5_out, not_6_out, not_7_out, not_8_out, not_9_out, not_10_out, not_11_out,
       not_12_out, not_13_out, not_14_out, not_15_out, not_16_out, not_17_out, not_18_out, not_19_out,
       not_20_out, not_21_out, not_22_out, not_23_out, not_24_out, not_25_out, not_26_out, not_27_out,
       not_28_out, not_29_out, not_30_out, not_31_out, not_32_out, not_33_out, not_34_out, not_35_out,
       not_36_out, or_1_out, or_9_out;

  not not_1 (not_1_out, A);
  not not_2 (not_2_out, B);
  not not_3 (not_3_out, D);
  not not_4 (not_4_out, C);
  not not_5 (not_5_out, B);
  not not_6 (not_6_out, not_5_out);
  not not_7 (not_7_out, A);
  not not_8 (not_8_out, C);
  not not_9 (not_9_out, A);
  not not_10 (not_10_out, D);
  not not_11 (not_11_out, B);
  not not_12 (not_12_out, C);
  not not_13 (not_13_out, D);
  not not_14 (not_14_out, B);
  not not_15 (not_15_out, A);
  not not_16 (not_16_out, C);
  and and_1 (and_1_out, B, D, not_1_out);
  and and_2 (and_2_out, not_1_out, C);
  and and_3 (and_3_out, not_2_out, not_3_out);
  and and_4 (and_4_out, not_2_out, not_4_out, A);
  not not_17 (not_17_out, C);
  not not_18 (not_18_out, B);
  not not_19 (not_19_out, D);
  not not_20 (not_20_out, A);
  and and_5 (and_5_out, A, not_5_out);
  and and_6 (and_6_out, not_6_out, not_7_out);
  and and_7 (and_7_out, not_7_out, not_8_out);
  and and_8 (and_8_out, not_7_out, D);
  and and_9 (and_9_out, not_9_out, not_10_out, C);
  and and_10 (and_10_out, not_11_out, C, D);
  and and_11 (and_11_out, A, not_12_out, not_13_out);
  and and_12 (and_12_out, not_12_out, not_13_out, not_14_out);
  and and_13 (and_13_out, not_15_out, B, not_16_out, D);
  and and_14 (and_14_out, not_17_out, not_18_out);
  and and_15 (and_15_out, not_18_out, not_19_out);
  and and_16 (and_16_out, not_17_out, not_19_out, not_20_out);
  and and_17 (and_17_out, not_20_out, C, D);
  or or_1 (or_1_out, and_9_out, and_10_out);
  and and_18 (and_18_out, not_14_out, A, D);
  not not_21 (not_21_out, C);
  or or_2 (a_2, and_1_out, and_2_out, and_3_out, and_4_out);
  or or_3 (b_2, and_14_out, and_15_out, and_16_out, and_17_out);
  or or_4 (c_2, and_5_out, and_6_out, and_7_out, and_8_out);
  or or_5 (d_2, or_1_out, and_11_out, and_12_out, and_18_out, and_13_out);
  not not_22 (not_22_out, B);
  not not_23 (not_23_out, D);
  not not_24 (not_24_out, A);
  not not_25 (not_25_out, B);
  not not_26 (not_26_out, A);
  not not_27 (not_27_out, C);
  not not_28 (not_28_out, D);
  not not_29 (not_29_out, B);
  not not_30 (not_30_out, C);
  not not_31 (not_31_out, D);
  not not_32 (not_32_out, B);
  not not_33 (not_33_out, A);
  not not_34 (not_34_out, C);
  not not_35 (not_35_out, D);
  not not_36 (not_36_out, A);
  and and_19 (and_19_out, not_22_out, not_23_out);
  and and_20 (and_20_out, not_23_out, not_24_out, C);
  and and_21 (and_21_out, A, not_21_out, not_23_out);
  and and_22 (and_22_out, A, not_22_out, C);
  and and_23 (and_23_out, A, not_25_out);
  and and_24 (and_24_out, not_26_out, not_27_out, B);
  and and_25 (and_25_out, not_26_out, B, not_28_out);
  and and_26 (and_26_out, not_29_out, not_30_out, not_31_out);
  and and_27 (and_27_out, A, not_32_out);
  and and_28 (and_28_out, not_32_out, C);
  and and_29 (and_29_out, not_33_out, B, not_34_out);
  and and_30 (and_30_out, B, not_34_out, not_35_out);
  and and_31 (and_31_out, not_36_out, C, not_35_out);
  or or_6 (out_9, and_19_out, and_20_out, and_21_out, and_22_out);
  or or_7 (f, and_23_out, and_24_out, and_25_out, and_26_out);
  or or_8 (g, and_27_out, and_28_out, and_29_out, or_9_out);
  or or_9 (or_9_out, and_30_out, and_31_out);

  // Notes on the sheet:
  //   A
  //   B
  //   C
  //   D
  //   A
  //   B
  //   C
  //   D
  //   C
  //   D
  //   D
  //   A
  //   B
  //   A
  //   B
  //   C
  //   e
endmodule
