// Logisim project dois lados OK.circ as structural Verilog: 1 circuit, main circuit main
module main (
  input  A,
  input  A_2,
  input  B,
  input  B_2,
  input  C,
  input  C_2,
  input  D,
  input  D_2
);

  wire and_1_out, and_2_out, and_3_out, and_4_out, and_5_out, and_6_out, and_7_out, and_8_out, and_9_out,
       and_10_out, and_11_out, and_12_out, and_13_out, and_14_out, and_15_out, and_16_out, and_17_out,
       and_18_out, and_19_out, and_20_out, and_21_out, and_22_out, and_23_out, and_24_out, and_25_out,
       and_26_out, and_27_out, and_28_out, and_29_out, and_30_out, and_31_out, and_32_out, and_33_out,
       and_34_out, and_35_out, and_36_out, and_37_out, and_38_out, and_39_out, and_40_out, and_41_out,
       and_42_out, and_43_out, and_44_out, and_45_out, and_46_out, and_47_out, and_48_out, and_49_out,
       and_50_out, and_51_out, and_52_out, and_53_out, and_54_out, and_55_out, and_56_out, and_57_out,
       and_58_out, and_59_out, and_60_out, and_61_out, and_62_out, not_1_out, not_2_out, not_3_out,
       not_4_out, not_5_out, not_6_out, not_7_out, not_8_out, not_9_out, not_10_out, not_11_out, not_12_out,
       not_13_out, not_14_out, not_15_out, not_16_out, not_17_out, not_18_out, not_19_out, not_20_out,
       not_21_out, not_22_out, not_23_out, not_24_out, not_25_out, not_26_out, not_27_out, not_28_out,
       not_29_out, not_30_out, not_31_out, not_32_out, not_33_out, not_34_out, not_35_out, not_36_out,
       not_37_out, not_38_out, not_39_out, not_40_out, not_41_out, not_42_out, not_43_out, not_44_out,
       not_45_out, not_46_out, not_47_out, not_48_out, not_49_out, not_50_out, not_51_out, not_52_out,
       not_53_out, not_54_out, not_55_out, not_56_out, not_57_out, not_58_out, not_59_out, not_60_out,
       not_61_out, not_62_out, not_63_out, not_64_out, not_65_out, not_66_out, not_67_out, not_68_out,
       not_69_out, not_70_out, not_71_out, not_72_out, or_1_out, or_2_out, or_3_out, or_4_out, or_5_out,
       or_6_out, or_7_out, or_8_out, or_9_out, or_10_out, or_11_out, or_12_out, or_13_out, or_14_out,
       or_15_out, or_16_out, or_17_out, or_18_out;

  not not_1 (not_1_out, A);
  not not_2 (not_2_out, B);
  not not_3 (not_3_out, D);
  not not_4 (not_4_out, C);
  not not_5 (not_5_out, B);
  not not_6 (not_6_out, not_5_out);
  not not_7 (not_7_out, A);
  not not_8 (not_8_out, C);
  not not_9 (not_9_out, A);
  not not_10 (not_10_out, D);
  not not_11 (not_11_out, B);
  not not_12 (not_12_out, C);
  not not_13 (not_13_out, D);
  not not_14 (not_14_out, B);
  not not_15 (not_15_out, A);
  not not_16 (not_16_out, C);
  and and_1 (and_1_out, B, D, not_1_out);
  and and_2 (and_2_out, not_1_out, C);
  and and_3 (and_3_out, not_2_out, not_3_out);
  and and_4 (and_4_out, not_2_out, not_4_out, A);
  not not_17 (not_17_out, C);
  not not_18 (not_18_out, B);
  not not_19 (not_19_out, D);
  not not_20 (not_20_out, A);
  and and_5 (and_5_out, A, not_5_out);
  and and_6 (and_6_out, not_6_out, not_7_out);
  and and_7 (and_7_out, not_7_out, not_8_out);
  and and_8 (and_8_out, not_7_out, D);
  and and_9 (and_9_out, not_9_out, not_10_out, C);
  and and_10 (and_10_out, not_11_out, C, D);
  and and_11 (and_11_out, A, not_12_out, not_13_out);
  and and_12 (and_12_out, not_12_out, not_13_out, not_14_out);
  and and_13 (and_13_out, not_15_out, B, not_16_out, D);
  and and_14 (and_14_out, not_17_out, not_18_out);
  and and_15 (and_15_out, not_18_out, not_19_out);
  and and_16 (and_16_out, not_17_out, not_19_out, not_20_out);
  and and_17 (and_17_out, not_20_out, C, D);
  or or_1 (or_1_out, and_9_out, and_10_out);
  and and_18 (and_18_out, not_14_out, A, D);
  not not_21 (not_21_out, C);
  or or_2 (or_2_out, and_1_out, and_2_out, and_3_out, and_4_out);
  _7_Segment_Display u_7_segment_display_1 (
    .g(or_8_out), .f(or_7_out), .a(or_2_out), .b(or_3_out), .e(or_6_out), .d(or_5_out), .c(or_4_out));  // open: dp
  or or_3 (or_3_out, and_14_out, and_15_out, and_16_out, and_17_out);
  or or_4 (or_4_out, and_5_out, and_6_out, and_7_out, and_8_out);
  or or_5 (or_5_out, or_1_out, and_11_out, and_12_out, and_18_out, and_13_out);
  not not_22 (not_22_out, B);
  not not_23 (not_23_out, D);
  not not_24 (not_24_out, A);
  not not_25 (not_25_out, B);
  not not_26 (not_26_out, A);
  not not_27 (not_27_out, C);
  not not_28 (not_28_out, D);
  not not_29 (not_29_out, B);
  not not_30 (not_30_out, C);
  not not_31 (not_31_out, D);
  not not_32 (not_32_out, B);
  not not_33 (not_33_out, A);
  not not_34 (not_34_out, C);
  not not_35 (not_35_out, D);
  not not_36 (not_36_out, A);
  and and_19 (and_19_out, not_22_out, not_23_out);
  and and_20 (and_20_out, not_23_out, not_24_out, C);
  and and_21 (and_21_out, A, not_21_out, not_23_out);
  and and_22 (and_22_out, A, not_22_out, C);
  and and_23 (and_23_out, A, not_25_out);
  and and_24 (and_24_out, not_26_out, not_27_out, B);
  and and_25 (and_25_out, not_26_out, B, not_28_out);
  and and_26 (and_26_out, not_29_out, not_30_out, not_31_out);
  and and_27 (and_27_out, A, not_32_out);
  and and_28 (and_28_out, not_32_out, C);
  and and_29 (and_29_out, not_33_out, B, not_34_out);
  and and_30 (and_30_out, B, not_34_out, not_35_out);
  and and_31 (and_31_out, not_36_out, C, not_35_out);
  or or_6 (or_6_out, and_19_out, and_20_out, and_21_out, and_22_out);
  or or_7 (or_7_out, and_23_out, and_24_out, and_25_out, and_26_out);
  or or_8 (or_8_out, and_27_out, and_28_out, and_29_out, or_9_out);
  or or_9 (or_9_out, and_30_out, and_31_out);
  not not_37 (not_37_out, A_2);
  not not_38 (not_38_out, B_2);
  not not_39 (not_39_out, C_2);
  and and_32 (and_32_out, B_2, D_2, not_37_out);
  and and_33 (and_33_out, not_37_out, C_2);
  not not_40 (not_40_out, B_2);
  not not_41 (not_41_out, D_2);
  and and_34 (and_34_out, not_40_out, not_42_out, A_2);
  not not_42 (not_42_out, C_2);
  not not_43 (not_43_out, C_2);
  not not_44 (not_44_out, B_2);
  not not_45 (not_45_out, D_2);
  not not_46 (not_46_out, A_2);
  not not_47 (not_47_out, not_38_out);
  not not_48 (not_48_out, A_2);
  not not_49 (not_49_out, A_2);
  not not_50 (not_50_out, D_2);
  not not_51 (not_51_out, B_2);
  not not_52 (not_52_out, C_2);
  not not_53 (not_53_out, D_2);
  not not_54 (not_54_out, B_2);
  not not_55 (not_55_out, A_2);
  not not_56 (not_56_out, C_2);
  and and_35 (and_35_out, not_40_out, not_41_out);
  and and_36 (and_36_out, not_43_out, not_44_out);
  and and_37 (and_37_out, not_44_out, not_45_out);
  and and_38 (and_38_out, not_43_out, not_45_out, not_46_out);
  and and_39 (and_39_out, not_46_out, C_2, D_2);
  and and_40 (and_40_out, A_2, not_38_out);
  and and_41 (and_41_out, not_47_out, not_48_out);
  and and_42 (and_42_out, not_48_out, not_39_out);
  and and_43 (and_43_out, not_48_out, D_2);
  and and_44 (and_44_out, not_49_out, not_50_out, C_2);
  or or_10 (or_10_out, and_44_out, and_45_out);
  and and_45 (and_45_out, not_51_out, C_2, D_2);
  and and_46 (and_46_out, A_2, not_52_out, not_53_out);
  and and_47 (and_47_out, not_52_out, not_53_out, not_54_out);
  and and_48 (and_48_out, not_54_out, A_2, D_2);
  and and_49 (and_49_out, not_55_out, B_2, not_56_out, D_2);
  or or_11 (or_11_out, and_32_out, and_33_out, and_35_out, and_34_out);
  or or_12 (or_12_out, and_36_out, and_37_out, and_38_out, and_39_out);
  or or_13 (or_13_out, and_40_out, and_41_out, and_42_out, and_43_out);
  or or_14 (or_14_out, or_10_out, and_46_out, and_47_out, and_48_out, and_49_out);
  not not_57 (not_57_out, B_2);
  not not_58 (not_58_out, D_2);
  not not_59 (not_59_out, A_2);
  not not_60 (not_60_out, C_2);
  not not_61 (not_61_out, B_2);
  not not_62 (not_62_out, A_2);
  not not_63 (not_63_out, C_2);
  not not_64 (not_64_out, D_2);
  not not_65 (not_65_out, B_2);
  not not_66 (not_66_out, C_2);
  not not_67 (not_67_out, D_2);
  not not_68 (not_68_out, B_2);
  not not_69 (not_69_out, A_2);
  not not_70 (not_70_out, C_2);
  not not_71 (not_71_out, D_2);
  not not_72 (not_72_out, A_2);
  _7_Segment_Display u_7_segment_display_2 (
    .g(or_17_out), .f(or_16_out), .a(or_11_out), .b(or_12_out), .e(or_15_out), .d(or_14_out), .c(or_13_out));  // open: dp
  and and_50 (and_50_out, not_57_out, not_58_out);
  and and_51 (and_51_out, not_58_out, not_59_out, C_2);
  and and_52 (and_52_out, A_2, not_60_out, not_58_out);
  and and_53 (and_53_out, A_2, not_57_out, C_2);
  and and_54 (and_54_out, A_2, not_61_out);
  and and_55 (and_55_out, not_62_out, not_63_out, B_2);
  and and_56 (and_56_out, not_62_out, B_2, not_64_out);
  and and_57 (and_57_out, not_65_out, not_66_out, not_67_out);
  and and_58 (and_58_out, A_2, not_68_out);
  and and_59 (and_59_out, not_68_out, C_2);
  and and_60 (and_60_out, not_69_out, B_2, not_70_out);
  and and_61 (and_61_out, B_2, not_70_out, not_71_out);
  and and_62 (and_62_out, not_72_out, C_2, not_71_out);
  or or_15 (or_15_out, and_50_out, and_51_out, and_52_out, and_53_out);
  or or_16 (or_16_out, and_54_out, and_55_out, and_56_out, and_57_out);
  or or_17 (or_17_out, and_58_out, and_59_out, and_60_out, or_18_out);
  or or_18 (or_18_out, and_61_out, and_62_out);

  // Notes on the sheet:
  //   B
  //   A
  //   B
  //   C
  //   D
  //   A
  //   B
  //   C
  //   D
  //   C
  //   D
  //   D
  //   A
  //   B
  //   A
  //   B
  //   C
  //   a
  //   b
  //   c
  //   d
  //   e
  //   f
  //   g
  //   A
  //   B
  //   C
  //   D
  //   A
  //   B
  //   C
  //   D
  //   D
  //   A
  //   B
  //   C
  //   A
  //   B
  //   C
  //   D
  //   a
  //   b
  //   c
  //   d
  //   e
  //   f
  //   g
endmodule
