// Logisim project trab ga.circ as structural Verilog: 1 circuit, main circuit main
module main (
  input  A,
  input  B,
  input  C,
  input  D
);

  wire and_1_out, and_2_out, and_3_out, and_4_out, and_5_out, and_6_out, and_7_out, and_8_out, and_9_out,
       and_10_out, and_11_out, and_12_out, and_13_out, and_14_out, and_15_out, and_16_out, and_17_out,
       and_18_out, and_19_out, and_20_out, and_21_out, and_22_out, not_1_out, not_2_out, not_3_out,
       not_4_out, not_5_out, not_6_out, not_7_out, not_8_out, not_9_out, not_10_out, not_11_out, not_12_out,
       not_13_out, not_14_out, not_15_out, not_16_out, not_17_out, not_18_out, not_19_out, not_20_out,
       not_21_out, not_22_out, not_23_out, not_24_out, or_1_out, or_2_out, or_3_out, or_4_out, or_5_out,
       or_6_out;

  not not_1 (not_1_out, B);
  not not_2 (not_2_out, C);
  not not_3 (not_3_out, A);
  not not_4 (not_4_out, B);
  not not_5 (not_5_out, D);
  not not_6 (not_6_out, C);
  not not_7 (not_7_out, C);
  not not_8 (not_8_out, B);
  not not_9 (not_9_out, D);
  not not_10 (not_10_out, A);
  not not_11 (not_11_out, not_1_out);
  not not_12 (not_12_out, A);
  not not_13 (not_13_out, A);
  not not_14 (not_14_out, D);
  not not_15 (not_15_out, B);
  not not_16 (not_16_out, C);
  not not_17 (not_17_out, D);
  not not_18 (not_18_out, B);
  not not_19 (not_19_out, A);
  not not_20 (not_20_out, C);
  and and_1 (and_1_out, B, D, not_3_out);
  and and_2 (and_2_out, not_3_out, C);
  and and_3 (and_3_out, not_4_out, not_5_out);
  and and_4 (and_4_out, not_4_out, not_6_out, A);
  and and_5 (and_5_out, not_7_out, not_8_out);
  and and_6 (and_6_out, not_8_out, not_9_out);
  and and_7 (and_7_out, not_7_out, not_9_out, not_10_out);
  and and_8 (and_8_out, not_10_out, C, D);
  and and_9 (and_9_out, A, not_1_out);
  and and_10 (and_10_out, not_11_out, not_12_out);
  and and_11 (and_11_out, not_12_out, not_2_out);
  and and_12 (and_12_out, not_12_out, D);
  and and_13 (and_13_out, not_13_out, not_14_out, C);
  or or_1 (or_1_out, and_13_out, and_14_out);
  and and_14 (and_14_out, not_15_out, C, D);
  and and_15 (and_15_out, A, not_16_out, not_17_out);
  and and_16 (and_16_out, not_16_out, not_17_out, not_18_out);
  and and_17 (and_17_out, not_18_out, A, D);
  and and_18 (and_18_out, not_19_out, B, not_20_out, D);
  or or_2 (or_2_out, and_1_out, and_2_out, and_3_out, and_4_out);
  or or_3 (or_3_out, and_9_out, and_10_out, and_11_out, and_12_out);
  or or_4 (or_4_out, or_1_out, and_15_out, and_16_out, and_17_out, and_18_out);
  not not_21 (not_21_out, B);
  not not_22 (not_22_out, D);
  not not_23 (not_23_out, A);
  not not_24 (not_24_out, C);
  _7_Segment_Display u_7_segment_display_1 (
    .a(or_2_out), .b(or_5_out), .e(or_6_out), .d(or_4_out), .c(or_3_out));  // open: g, f, dp
  or or_5 (or_5_out, and_5_out, and_6_out, and_7_out, and_8_out);
  and and_19 (and_19_out, not_21_out, not_22_out);
  and and_20 (and_20_out, not_22_out, not_23_out, C);
  and and_21 (and_21_out, A, not_24_out, not_22_out);
  and and_22 (and_22_out, A, not_21_out, C);
  or or_6 (or_6_out, and_19_out, and_20_out, and_21_out, and_22_out);

  // Notes on the sheet:
  //   A
  //   B
  //   C
  //   D
  //   A
  //   B
  //   C
  //   D
endmodule
